// Logisim project decoder.circ as structural Verilog: 1 circuit, main circuit main
module main (
  input  G1,
  input  G2,
  input  D2,
  input  D1,
  input  D0,
  output nY0,
  output nY1,
  output nY2,
  output nY3,
  output nY4,
  output nY5,
  output nY6,
  output nY7
);

  wire and_1_out, and_2_out, and_3_out, and_4_out, and_5_out, and_6_out, and_7_out, and_8_out, not_1_out,
       not_2_out, not_3_out, not_4_out;

  not not_1 (not_1_out, D2);
  not not_2 (not_2_out, D1);
  not not_3 (not_3_out, D0);
  not not_4 (not_4_out, G2);
  and and_1 (and_1_out, not_4_out, G1, not_1_out, not_2_out, not_3_out);
  and and_2 (and_2_out, not_4_out, G1, not_1_out, not_2_out, D0);
  and and_3 (and_3_out, not_4_out, G1, not_1_out, D1, not_3_out);
  and and_4 (and_4_out, not_4_out, G1, not_1_out, D1, D0);
  and and_5 (and_5_out, not_4_out, G1, D2, not_2_out, not_3_out);
  and and_6 (and_6_out, not_4_out, G1, D2, not_2_out, D0);
  and and_7 (and_7_out, not_4_out, G1, D2, D1, not_3_out);
  and and_8 (and_8_out, not_4_out, G1, D2, D1, D0);
  not not_5 (nY0, and_1_out);
  not not_6 (nY1, and_2_out);
  not not_7 (nY2, and_3_out);
  not not_8 (nY3, and_4_out);
  not not_9 (nY4, and_5_out);
  not not_10 (nY5, and_6_out);
  not not_11 (nY6, and_7_out);
  not not_12 (nY7, and_8_out);
endmodule
