// Logisim project encoder83.circ as structural Verilog: 1 circuit, main circuit main
module main (
  input  D7,
  input  D6,
  input  D5,
  input  D4,
  input  D3,
  input  D2,
  input  D1,
  input  D0,
  output Y2,
  output Y1,
  output Y0
);

  wire and_1_out, and_2_out, and_3_out, and_4_out, and_5_out, and_6_out, and_7_out, and_8_out, and_9_out,
       and_10_out, and_11_out, and_12_out, and_13_out, and_14_out, and_15_out, and_16_out, and_17_out,
       and_18_out, and_19_out, and_20_out, and_21_out, and_22_out, and_23_out, and_24_out, and_25_out,
       and_26_out, and_27_out, and_28_out, and_29_out, and_30_out, and_31_out, and_32_out, and_33_out,
       and_34_out, and_35_out, and_36_out, not_1_out, not_2_out, not_3_out, not_4_out, not_5_out, not_6_out,
       not_7_out, not_8_out, not_9_out, not_10_out, not_11_out, not_12_out, not_13_out, not_14_out,
       not_15_out, not_16_out;

  not not_1 (not_1_out, D7);
  not not_2 (not_2_out, D6);
  not not_3 (not_3_out, D5);
  not not_4 (not_4_out, D4);
  not not_5 (not_5_out, D3);
  not not_6 (not_6_out, D2);
  not not_7 (not_7_out, D1);
  not not_8 (not_8_out, D0);
  and and_1 (and_1_out, D7, not_2_out, not_3_out, not_4_out);
  and and_2 (and_2_out, not_5_out, not_6_out, not_7_out, not_8_out);
  and and_3 (and_3_out, not_1_out, D6, not_3_out, not_4_out);
  and and_4 (and_4_out, not_5_out, not_6_out, not_7_out, not_8_out);
  and and_5 (and_5_out, not_1_out, not_2_out, D5, not_4_out);
  and and_6 (and_6_out, not_5_out, not_6_out, not_7_out, not_8_out);
  and and_7 (and_7_out, not_1_out, not_2_out, not_3_out, D4);
  and and_8 (and_8_out, not_5_out, not_6_out, not_7_out, not_8_out);
  and and_9 (and_9_out, D7, not_2_out, not_3_out, not_4_out);
  and and_10 (and_10_out, not_5_out, not_6_out, not_7_out, not_8_out);
  and and_11 (and_11_out, not_1_out, D6, not_3_out, not_4_out);
  and and_12 (and_12_out, not_5_out, not_6_out, not_7_out, not_8_out);
  and and_13 (and_13_out, not_1_out, not_2_out, not_3_out, not_4_out);
  and and_14 (and_14_out, D3, not_6_out, not_7_out, not_8_out);
  and and_15 (and_15_out, not_1_out, not_2_out, not_3_out, not_4_out);
  and and_16 (and_16_out, not_5_out, D2, not_8_out, not_7_out);
  and and_17 (and_17_out, and_1_out, and_2_out);
  and and_18 (and_18_out, and_3_out, and_4_out);
  and and_19 (and_19_out, and_5_out, and_6_out);
  and and_20 (and_20_out, and_7_out, and_8_out);
  and and_21 (and_21_out, and_9_out, and_10_out);
  and and_22 (and_22_out, and_11_out, and_12_out);
  and and_23 (and_23_out, and_13_out, and_14_out);
  and and_24 (and_24_out, and_15_out, and_16_out);
  or or_1 (Y2, and_17_out, and_18_out, and_19_out, and_20_out);
  or or_2 (Y1, and_21_out, and_22_out, and_23_out, and_24_out);
  not not_9 (not_9_out, D7);
  not not_10 (not_10_out, D6);
  not not_11 (not_11_out, D5);
  not not_12 (not_12_out, D4);
  not not_13 (not_13_out, D3);
  not not_14 (not_14_out, D2);
  not not_15 (not_15_out, D1);
  not not_16 (not_16_out, D0);
  and and_25 (and_25_out, D7, not_10_out, not_11_out, not_12_out);
  and and_26 (and_26_out, not_13_out, not_14_out, not_15_out, not_16_out);
  and and_27 (and_27_out, not_9_out, not_10_out, D5, not_12_out);
  and and_28 (and_28_out, not_13_out, not_14_out, not_15_out, not_16_out);
  and and_29 (and_29_out, not_9_out, not_10_out, not_11_out, not_12_out);
  and and_30 (and_30_out, D3, not_14_out, not_15_out, not_16_out);
  and and_31 (and_31_out, not_9_out, not_10_out, not_11_out, not_12_out);
  and and_32 (and_32_out, not_13_out, not_14_out, not_16_out, D1);
  and and_33 (and_33_out, and_25_out, and_26_out);
  and and_34 (and_34_out, and_27_out, and_28_out);
  and and_35 (and_35_out, and_29_out, and_30_out);
  and and_36 (and_36_out, and_31_out, and_32_out);
  or or_3 (Y0, and_33_out, and_34_out, and_35_out, and_36_out);

  // Notes on the sheet:
  //   D0
  //   Y2
  //   D7
  //   D6
  //   D5
  //   D4
  //   D3
  //   D2
  //   D1
  //   Y1
  //   Y0
endmodule
