// Logisim project jk_ff.circ as structural Verilog: 1 circuit, main circuit main
module main (
  input  J,
  input  CLK,
  input  K,
  output Q,
  output nQ
);

  wire and_1_out, and_2_out, not_1_out, not_2_out, not_3_out, not_4_out, not_5_out, not_6_out;

  and and_1 (and_1_out, J, nQ, CLK);
  and and_2 (and_2_out, CLK, Q, K);
  not not_1 (not_1_out, and_1_out);
  not not_2 (not_2_out, and_2_out);
  not not_3 (not_3_out, not_1_out);
  not not_4 (not_4_out, nQ);
  not not_5 (not_5_out, Q);
  not not_6 (not_6_out, not_2_out);
  or or_1 (Q, not_3_out, not_4_out);
  or or_2 (nQ, not_5_out, not_6_out);
endmodule
