// Logisim project sr_ff.circ as structural Verilog: 1 circuit, main circuit main
module main (
  input  in_1,
  input  in_2,
  input  in_3,
  output out_4,
  output out_5
);

  wire and_1_out, and_2_out, not_1_out, not_2_out, not_3_out, not_4_out, not_5_out, not_6_out;

  and and_1 (and_1_out, in_1, in_2);
  and and_2 (and_2_out, in_2, in_3);
  not not_1 (not_1_out, and_1_out);
  not not_2 (not_2_out, and_2_out);
  not not_3 (not_3_out, not_1_out);
  not not_4 (not_4_out, out_5);
  not not_5 (not_5_out, out_4);
  not not_6 (not_6_out, not_2_out);
  or or_1 (out_4, not_3_out, not_4_out);
  or or_2 (out_5, not_5_out, not_6_out);
endmodule
