// Logisim project 多路控制加法器.circ as structural Verilog: 1 circuit, main circuit main
module main (
  input  [7:0] in_1,
  output reg_C,
  output [7:0] out_3
);

  wire adder_1_cout, and_1_out, and_2_out, and_3_out, clock_1_out, d_ff_1_qn, d_ff_2_qn, multiplexer_1_out,
       multiplexer_2_out, nor_1_out, not_1_out, not_2_out, not_3_out, not_4_out, or_1_out, xor_1_out;
  wire [1:0] d_ff_1_q;
  wire [7:0] adder_1_out, controlled_buffer_1_out, register_1_q;

  Clock clock_1 (.out(clock_1_out));
  not not_1 (not_1_out, 1'b1);
  not not_2 (not_2_out, 1'b1);
  Multiplexer #(.select(2)) multiplexer_1 (
    .in0(not_1_out), .in1(1'b1), .in2(1'b1), .in3(1'b1), .out(multiplexer_1_out), .sel(d_ff_1_q));  // open: en
  Multiplexer #(.select(2)) multiplexer_2 (
    .in0(1'b1), .in1(1'b1), .in2(1'b1), .in3(not_2_out), .out(multiplexer_2_out), .sel(d_ff_1_q));  // open: en
  D_Flip_Flop d_ff_1 (
    .clk(clock_1_out), .D(multiplexer_1_out), .Q(d_ff_1_q[0]), .Qn(d_ff_1_qn));  // open: preset, en, reset
  D_Flip_Flop d_ff_2 (
    .clk(clock_1_out), .D(multiplexer_2_out), .Q(d_ff_1_q[1]), .Qn(d_ff_2_qn));  // open: preset, en, reset
  not not_3 (not_3_out, clock_1_out);
  and and_1 (and_1_out, d_ff_1_q[0], d_ff_1_q[1]);
  and and_2 (and_2_out, d_ff_1_qn, d_ff_2_qn);
  or or_1 (or_1_out, and_1_out, and_2_out);
  xor xor_1 (xor_1_out, d_ff_1_q[0], d_ff_1_q[1]);
  and and_3 (and_3_out, d_ff_1_q[0], d_ff_2_qn);
  nor nor_1 (nor_1_out, d_ff_1_q[0], d_ff_1_q[1]);
  Register register_1 (.D(in_1), .en(or_1_out), .Q(register_1_q), .clk(not_3_out));  // open: clr
  Register register_2 (.D(adder_1_out), .en(xor_1_out), .Q(out_3), .clk(not_3_out));  // open: clr
  assign controlled_buffer_1_out = and_3_out ? out_3 : 8'bz;  // Controlled_Buffer controlled_buffer_1
  not not_4 (not_4_out, 1'b1);
  Adder adder_1 (
    .a(register_1_q), .b(controlled_buffer_1_out), .out(adder_1_out), .cin(not_4_out), .cout(adder_1_cout));
  Register #(.width(1)) register_3 (.D(adder_1_cout), .en(and_3_out), .Q(reg_C), .clk(not_3_out), .clr(nor_1_out));

  // Notes on the sheet:
  //   B
  //   A
  //   LDA
  //   LDB
  //   ADD
  //   ~CLR
  //   reg A
  //   reg B
endmodule
