// Logisim project 多路控制比较器.circ as structural Verilog: 1 circuit, main circuit main
module main (
  input  [7:0] in_1
);

  wire and_1_out, and_2_out, clock_1_out, comparator_1_gt, d_ff_1_qn, d_ff_2_qn, multiplexer_1_out,
       multiplexer_2_out, not_1_out, not_2_out, not_3_out, xnor_1_out;
  wire [1:0] d_ff_2_q;
  wire [7:0] controlled_buffer_1_out, controlled_buffer_2_out, register_1_q, register_2_q;

  not not_1 (not_1_out, 1'b1);
  not not_2 (not_2_out, 1'b1);
  Multiplexer #(.select(2)) multiplexer_1 (
    .in0(not_1_out), .in1(1'b1), .in2(comparator_1_gt), .in3(1'b1), .out(multiplexer_1_out), .sel(d_ff_2_q));  // open: en
  Multiplexer #(.select(2)) multiplexer_2 (
    .in0(1'b1), .in1(1'b1), .in2(1'b1), .in3(not_2_out), .out(multiplexer_2_out), .sel(d_ff_2_q));  // open: en
  Clock clock_1 (.out(clock_1_out));
  D_Flip_Flop d_ff_1 (
    .clk(clock_1_out), .D(multiplexer_1_out), .Q(d_ff_2_q[1]), .Qn(d_ff_1_qn));  // open: preset, en, reset
  D_Flip_Flop d_ff_2 (
    .clk(clock_1_out), .D(multiplexer_2_out), .Q(d_ff_2_q[0]), .Qn(d_ff_2_qn));  // open: preset, en, reset
  xnor xnor_1 (xnor_1_out, d_ff_2_q[1], d_ff_2_q[0]);
  and and_1 (and_1_out, d_ff_2_q[0], d_ff_1_qn);
  and and_2 (and_2_out, d_ff_2_q[1], d_ff_2_qn);
  not not_3 (not_3_out, clock_1_out);
  Register register_1 (.D(in_1), .en(xnor_1_out), .Q(register_1_q), .clk(not_3_out));  // open: clr
  Register register_2 (.D(register_1_q), .en(and_1_out), .Q(register_2_q), .clk(not_3_out));  // open: clr
  assign controlled_buffer_1_out = and_2_out ? register_2_q : 8'bz;  // Controlled_Buffer controlled_buffer_1
  assign controlled_buffer_2_out = and_2_out ? register_1_q : 8'bz;  // Controlled_Buffer controlled_buffer_2
  Comparator comparator_1 (
    .a(controlled_buffer_1_out), .b(controlled_buffer_2_out), .gt(comparator_1_gt));  // open: eq, lt

  // Notes on the sheet:
  //   LDB
  //   LDA
  //   CAP
endmodule
