// Logisim project 定序型加法器.circ as structural Verilog: 1 circuit, main circuit main
module main (
  input  in_1,
  input  [7:0] in_2,
  output reg_C,
  output [7:0] out_4
);

  wire adder_1_cout, clock_1_out, d_ff_1_q, d_ff_2_q, d_ff_3_q, d_ff_4_q, nor_1_out, not_1_out, not_2_out,
       or_1_out, or_2_out, or_3_out;
  wire [7:0] adder_1_out, controlled_buffer_1_out, register_1_q;

  Clock clock_1 (.out(clock_1_out));
  nor nor_1 (nor_1_out, d_ff_1_q, d_ff_2_q, d_ff_3_q, d_ff_4_q);
  D_Flip_Flop d_ff_1 (.clk(clock_1_out), .D(nor_1_out), .Q(d_ff_1_q), .reset(in_1));  // open: Qn, preset, en
  or or_1 (or_1_out, d_ff_1_q, d_ff_3_q);
  or or_2 (or_2_out, d_ff_2_q, d_ff_4_q);
  D_Flip_Flop d_ff_2 (.clk(clock_1_out), .D(d_ff_1_q), .Q(d_ff_2_q), .reset(in_1));  // open: Qn, preset, en
  or or_3 (or_3_out, d_ff_2_q, d_ff_4_q);
  D_Flip_Flop d_ff_3 (.clk(clock_1_out), .D(or_3_out), .Q(d_ff_3_q), .reset(in_1));  // open: Qn, preset, en
  D_Flip_Flop d_ff_4 (.clk(clock_1_out), .D(d_ff_3_q), .Q(d_ff_4_q), .reset(in_1));  // open: Qn, preset, en
  not not_1 (not_1_out, clock_1_out);
  Register register_1 (.D(in_2), .en(or_1_out), .Q(register_1_q), .clk(not_1_out));  // open: clr
  Register register_2 (.D(adder_1_out), .en(or_2_out), .Q(out_4), .clk(not_1_out));  // open: clr
  assign controlled_buffer_1_out = d_ff_4_q ? out_4 : 8'bz;  // Controlled_Buffer controlled_buffer_1
  not not_2 (not_2_out, 1'b1);
  Adder adder_1 (
    .a(register_1_q), .b(controlled_buffer_1_out), .out(adder_1_out), .cin(not_2_out), .cout(adder_1_cout));
  Register #(.width(1)) register_3 (.D(adder_1_cout), .en(d_ff_4_q), .Q(reg_C), .clk(not_1_out), .clr(d_ff_1_q));

  // Notes on the sheet:
  //   Qa
  //   Qb
  //   LDA
  //   LDB
  //   ~CLR
  //   ADD
  //   Qc
  //   Qd
  //   reg A
  //   reg B
endmodule
