// Logisim project 定序型比较器.circ as structural Verilog: 1 circuit, main circuit main
module main (
  input  in_1,
  input  [7:0] in_2
);

  wire and_1_out, and_2_out, clock_1_out, comparator_1_gt, d_ff_1_q, d_ff_2_q, d_ff_3_q, d_ff_4_q,
       nand_1_out, nor_1_out, not_1_out, not_2_out, not_3_out, not_4_out, or_1_out, or_2_out;
  wire [7:0] controlled_buffer_1_out, controlled_buffer_2_out, register_1_q, register_2_q;

  Clock clock_1 (.out(clock_1_out));
  not not_1 (not_1_out, clock_1_out);
  nor nor_1 (nor_1_out, d_ff_1_q, d_ff_2_q, d_ff_3_q, d_ff_4_q);
  D_Flip_Flop d_ff_1 (.clk(clock_1_out), .D(nor_1_out), .Q(d_ff_1_q), .reset(in_1));  // open: Qn, preset, en
  not not_2 (not_2_out, comparator_1_gt);
  and and_1 (and_1_out, d_ff_4_q, not_2_out);
  or or_1 (or_1_out, d_ff_1_q, and_1_out);
  not not_3 (not_3_out, d_ff_1_q);
  not not_4 (not_4_out, d_ff_3_q);
  D_Flip_Flop d_ff_2 (.clk(clock_1_out), .D(or_1_out), .Q(d_ff_2_q), .reset(in_1));  // open: Qn, preset, en
  nand nand_1 (nand_1_out, not_3_out, not_4_out);
  and and_2 (and_2_out, d_ff_4_q, comparator_1_gt);
  D_Flip_Flop d_ff_3 (.clk(clock_1_out), .D(or_2_out), .Q(d_ff_3_q), .reset(in_1));  // open: Qn, preset, en
  or or_2 (or_2_out, d_ff_2_q, and_2_out);
  D_Flip_Flop d_ff_4 (.clk(clock_1_out), .D(d_ff_3_q), .Q(d_ff_4_q), .reset(in_1));  // open: Qn, preset, en
  Register register_1 (.D(in_2), .en(nand_1_out), .Q(register_1_q), .clk(not_1_out));  // open: clr
  Register register_2 (.D(register_1_q), .en(d_ff_2_q), .Q(register_2_q), .clk(not_1_out));  // open: clr
  assign controlled_buffer_1_out = d_ff_4_q ? register_2_q : 8'bz;  // Controlled_Buffer controlled_buffer_1
  assign controlled_buffer_2_out = d_ff_4_q ? register_1_q : 8'bz;  // Controlled_Buffer controlled_buffer_2
  Comparator comparator_1 (
    .a(controlled_buffer_1_out), .b(controlled_buffer_2_out), .gt(comparator_1_gt));  // open: eq, lt

  // Notes on the sheet:
  //   Qa
  //   Qb
  //   LDB
  //   LDA
  //   CAP
  //   Qc
  //   Qd
endmodule
