// Logisim project 4位mux.circ as structural Verilog: 1 circuit, main circuit main
module main (
  input  in_1,
  input  in_2,
  input  in_3,
  input  in_4,
  input  in_5,
  input  in_6,
  input  in_7,
  input  in_8,
  input  in_9,
  input  in_10,
  input  in_11,
  input  in_12,
  input  in_13,
  input  in_14,
  input  in_15,
  input  in_16,
  input  in_17,
  input  in_18,
  output out_19,
  output out_20,
  output out_21,
  output out_22
);

  wire and_1_out, and_2_out, and_3_out, and_4_out, and_5_out, and_6_out, and_7_out, and_8_out, and_9_out,
       and_10_out, and_11_out, and_12_out, and_13_out, and_14_out, and_15_out, and_16_out, not_1_out,
       not_2_out;

  not not_1 (not_1_out, in_6);
  not not_2 (not_2_out, in_5);
  and and_1 (and_1_out, in_7, not_1_out, not_2_out);
  and and_2 (and_2_out, in_8, in_6, not_2_out);
  and and_3 (and_3_out, in_9, in_5, not_1_out);
  and and_4 (and_4_out, in_10, in_6, in_5);
  and and_5 (and_5_out, not_1_out, not_2_out, in_11);
  and and_6 (and_6_out, in_6, not_2_out, in_12);
  and and_7 (and_7_out, in_5, not_1_out, in_13);
  and and_8 (and_8_out, in_6, in_5, in_14);
  or or_1 (out_19, and_1_out, and_2_out, and_3_out, and_4_out);
  or or_2 (out_21, and_5_out, and_6_out, and_7_out, and_8_out);
  and and_9 (and_9_out, not_1_out, out_19, in_4);
  and and_10 (and_10_out, out_19, in_6, in_3);
  and and_11 (and_11_out, not_1_out, in_5, in_2);
  and and_12 (and_12_out, in_1, in_6, in_5);
  and and_13 (and_13_out, not_1_out, out_19, in_15);
  and and_14 (and_14_out, in_16, out_19, in_6);
  and and_15 (and_15_out, not_1_out, in_5, in_17);
  and and_16 (and_16_out, in_5, in_6, in_18);
  or or_3 (out_20, and_9_out, and_10_out, and_11_out, and_12_out);
  or or_4 (out_22, and_13_out, and_14_out, and_15_out, and_16_out);
endmodule
