// Logisim project counter8.circ as structural Verilog: 1 circuit, main circuit main
module main (
  input  in_1,
  input  CLK,
  input  CLR,
  output Q2,
  output Q0,
  output Q1
);

  wire and_1_out, not_1_out;

  not not_1 (not_1_out, CLR);
  J_K_Flip_Flop j_k_ff_1 (.J(in_1), .clk(CLK), .K(in_1), .Q(Q0), .reset(not_1_out));  // open: Qn, preset, en
  J_K_Flip_Flop j_k_ff_2 (.J(Q0), .clk(CLK), .K(Q0), .Q(Q2), .reset(not_1_out));  // open: Qn, preset, en
  and and_1 (and_1_out, Q0, Q2);
  J_K_Flip_Flop j_k_ff_3 (.J(and_1_out), .clk(CLK), .K(and_1_out), .Q(Q1), .reset(not_1_out));  // open: Qn, preset, en

  // Notes on the sheet:
  //   Q0
  //   Q1
  //   Q2
endmodule
