// Logisim project 计数器型控制器.circ as structural Verilog: 1 circuit, main circuit main
module main (
  input  [7:0] in_1,
  output reg_C,
  output [7:0] out_3
);

  wire adder_1_cout, and_1_out, and_2_out, and_3_out, clock_1_out, d_ff_1_q, d_ff_1_qn, d_ff_2_q, d_ff_2_qn,
       nor_1_out, not_1_out, not_2_out, or_1_out, or_2_out, or_3_out, xor_1_out;
  wire [7:0] adder_1_out, controlled_buffer_1_out, register_1_q;

  Clock clock_1 (.out(clock_1_out));
  or or_1 (or_1_out, d_ff_1_q, d_ff_2_q);
  D_Flip_Flop d_ff_1 (.clk(clock_1_out), .D(or_1_out), .Q(d_ff_1_q), .Qn(d_ff_1_qn));  // open: preset, en, reset
  not not_1 (not_1_out, clock_1_out);
  or or_2 (or_2_out, d_ff_1_qn, d_ff_2_qn);
  and and_1 (and_1_out, d_ff_2_qn, d_ff_1_qn);
  and and_2 (and_2_out, d_ff_2_q, d_ff_1_q);
  D_Flip_Flop d_ff_2 (.clk(clock_1_out), .D(or_2_out), .Q(d_ff_2_q), .Qn(d_ff_2_qn));  // open: preset, en, reset
  or or_3 (or_3_out, and_1_out, and_2_out);
  xor xor_1 (xor_1_out, d_ff_2_q, d_ff_1_q);
  and and_3 (and_3_out, d_ff_2_qn, d_ff_1_q);
  nor nor_1 (nor_1_out, d_ff_2_q, d_ff_1_q);
  Register register_1 (.D(in_1), .en(or_3_out), .Q(register_1_q), .clk(not_1_out));  // open: clr
  Register register_2 (.D(adder_1_out), .en(xor_1_out), .Q(out_3), .clk(not_1_out));  // open: clr
  assign controlled_buffer_1_out = and_3_out ? out_3 : 8'bz;  // Controlled_Buffer controlled_buffer_1
  not not_2 (not_2_out, 1'b1);
  Adder adder_1 (
    .a(register_1_q), .b(controlled_buffer_1_out), .out(adder_1_out), .cin(not_2_out), .cout(adder_1_cout));
  Register #(.width(1)) register_3 (.D(adder_1_cout), .en(and_3_out), .Q(reg_C), .clk(not_1_out), .clr(nor_1_out));

  // Notes on the sheet:
  //   B
  //   A
  //   LDA
  //   LDB
  //   ADD
  //   ~CLR
  //   reg A
  //   reg B
endmodule
