// Logisim project 综合实验计时模块控制器demo.circ as structural Verilog: 1 circuit, main circuit main
module main (
  input  in_1,
  output RSTA,
  output RSTB,
  output ADDA,
  output ADDB,
  output CMPA_9,
  output CMPB_5
);

  wire and_1_out, and_2_out, and_3_out, and_4_out, and_5_out, and_6_out, and_7_out, clock_1_out, d_ff_1_q,
       d_ff_1_qn, d_ff_2_q, d_ff_2_qn, d_ff_3_q, d_ff_3_qn, not_1_out, not_2_out, not_3_out, or_1_out,
       xor_1_out;

  not not_1 (not_1_out, d_ff_3_q);
  not not_2 (not_2_out, d_ff_2_q);
  not not_3 (not_3_out, d_ff_1_qn);
  and and_1 (and_1_out, not_1_out, not_2_out);
  and and_2 (and_2_out, not_2_out, not_3_out);
  and and_3 (and_3_out, d_ff_1_qn, d_ff_3_q, d_ff_2_q);
  and and_4 (and_4_out, d_ff_1_qn, d_ff_3_q, in_1);
  and and_5 (and_5_out, not_3_out, d_ff_2_q, in_1);
  xor xor_1 (xor_1_out, d_ff_2_q, d_ff_3_q);
  and and_6 (and_6_out, d_ff_1_qn, xor_1_out);
  or or_1 (or_1_out, and_1_out, and_2_out, and_3_out, and_4_out, and_5_out);
  and and_7 (and_7_out, d_ff_2_q, d_ff_3_qn);
  D_Flip_Flop d_ff_1 (.clk(clock_1_out), .D(and_7_out), .Q(d_ff_1_q), .Qn(d_ff_1_qn));  // open: preset, en, reset
  D_Flip_Flop d_ff_2 (.clk(clock_1_out), .D(and_6_out), .Q(d_ff_2_q), .Qn(d_ff_2_qn));  // open: preset, en, reset
  D_Flip_Flop d_ff_3 (.clk(clock_1_out), .D(or_1_out), .Q(d_ff_3_q), .Qn(d_ff_3_qn));  // open: preset, en, reset
  Clock clock_1 (.out(clock_1_out));
  and and_8 (RSTA, d_ff_1_qn, d_ff_3_qn);
  and and_9 (RSTB, d_ff_2_qn, d_ff_3_qn);
  and and_10 (ADDA, d_ff_1_qn, d_ff_2_q, d_ff_3_q);
  and and_11 (ADDB, d_ff_1_q, d_ff_2_qn, d_ff_3_q);
  and and_12 (CMPA_9, d_ff_1_qn, d_ff_2_qn, d_ff_3_q);
  and and_13 (CMPB_5, d_ff_1_q, d_ff_2_q, d_ff_3_qn);

  // Notes on the sheet:
  //   C
  //   B
  //   A
  //   ~C
  //   B
  //   ~B
  //   A
  //   ~A
  //   C
endmodule
